# Fritzing sketch hms_pcb (saved by Fritzing 0.9.10b)
breadboards: 1

parts:
  Soil_Moisture = Soil Moisture Sensor
  7_Segment1 = 7 Segment Display
  7_Segment2 = 7 Segment Display
  U3 = Hirose DF13 Series Header [part_number=DF13#-3P-1.25V package=DF13C-3P-1.25V]
  U4 = Hirose DF13 Series Header [part_number=DF13#-2P-1.25V package=DF13C-2P-1.25V]
  S2 = Round Pushbutton
  U5 = Hirose DF13 Series Header [part_number=DF13#-2P-1.25V package=DF13C-2P-1.25V]
  S3 = Round Pushbutton
  U1 = HD74LS48P [package=dil16]
  WeMos_D1_Mini1 = WeMos D1 Mini
  R1 = Resistor [tolerance=±5% power=0.25 resistance=10k package=THT]
  U2 = HD74LS48P [package=dil16]

nets:
  VCC: Soil_Moisture.VCC, U3.2, U5.1, S3.leg1, U1.VCC, WeMos_D1_Mini1.3V3, R1.Pin_0, U2.VCC
  GND: Soil_Moisture.GND, 7_Segment1.common_cathode, 7_Segment2.common_cathode, U3.1, U4.2, S2.leg0, U5.2, U1.GND, WeMos_D1_Mini1.G, U2.GND
  N1: Soil_Moisture.SIG, U3.3, WeMos_D1_Mini1.A0
  N2: 7_Segment1.Segment_E, U1.e
  N3: 7_Segment1.Segment_D, U1.d
  N4: 7_Segment1.Segment_C, U1.c
  N5: 7_Segment1.Segment_B, U1.b
  N6: 7_Segment1.Segment_A, U1.a
  N7: 7_Segment1.Segment_F, U1.f
  N8: 7_Segment1.Segment_G, U1.g
  N9: 7_Segment2.Segment_E, U2.e
  N10: 7_Segment2.Segment_D, U2.d
  N11: 7_Segment2.Segment_C, U2.c
  N12: 7_Segment2.Segment_B, U2.b
  N13: 7_Segment2.Segment_A, U2.a
  N14: 7_Segment2.Segment_F, U2.f
  N15: 7_Segment2.Segment_G, U2.g
  N16: U4.1, S2.leg1, WeMos_D1_Mini1.D8, R1.Pin_1
  3.3V: S3.leg0
  N17: U1.B, WeMos_D1_Mini1.D5
  N18: U1.C, WeMos_D1_Mini1.D6
  N19: U1.D, WeMos_D1_Mini1.D7
  N20: U1.A, WeMos_D1_Mini1.D0
  N21: WeMos_D1_Mini1.D1, U2.A
  N22: WeMos_D1_Mini1.D2, U2.B
  N23: WeMos_D1_Mini1.D3, U2.C
  N24: WeMos_D1_Mini1.D4, U2.D

custom parts:
  Round Pushbutton: A generic pushbutton.
  HD74LS48P: BCD to 7-seg decoder/driver
